// Logisim project nand2tetris.circ as structural Verilog
module my_or (
  input  ain,
  input  bin,
  output myout
);

  wire nand_1_out, nand_2_out;

  nand nand_1 (nand_1_out, ain, ain);
  nand nand_2 (nand_2_out, bin, bin);
  nand nand_3 (myout, nand_1_out, nand_2_out);
endmodule

module my_not (
  input  myin,
  output myout
);

  nand nand_1 (myout, myin, myin);
endmodule
